# Fritzing sketch שרטוט (saved by Fritzing 0.8.7b)
breadboards: 1

parts:
  Part1 = Arduino Uno (Rev3)
  J1 = Basic Servo
  Part2 = SRF05 Ultrasonic Rangefinder  # not connected
  LED1 = LED - 5mm [color="Yellow (585nm)" package="5 mm [THT]"]
  R1 = Resistor [tolerance=±5% resistance=220 package=THT]
  VCC1 = Battery block 9V  # not connected
  S1 = Pushbutton [package="[THT]"]
  R2 = Resistor [tolerance=±5% resistance=10 package=THT]

nets:
  N1: Part1.D10_PWM/SS, R1.Pin_0
  N2: Part1.D4, Part1.5V, S1.Pin_1, S1.Pin_2, S1.Pin_3, S1.Pin_4, R2.Pin_0
  N3: Part1.D7, J1.pulse
  3V3: Part1.3V3, J1.vcc
  GND: Part1.GND, J1.gnd, LED1.cathode, R2.Pin_1
  N4: LED1.anode, R1.Pin_1
